// Digital circuit CS_Lab3_Part5.dig as structural Verilog
module CS_Lab3_Part5 (
  input  CLK,
  input  [9:0] Input
);

  wire ALU_en_flag, ALU_Type, and_1_out, and_5_out, CND_en_flag, CND_out, comparator_1_eq, comparator_2_eq,
       IMM_en_flag, MOV_en_flag, not_1_out, not_2_out, NotCND;
  wire [1:0] Data_in_selector;
  wire [3:0] multiplexer_2_out, multiplexer_3_out;
  wire [7:0] IMM_value;
  wire [9:0] add_1_s, add_2_s, ALU_result, DATA_IN_REG, multiplexer_1_out, multiplexer_4_out, PC_q, REG_OUT1,
       REG_OUT2, register_1_q, sub_1_s;

  Add #(.Bits(10)) add_1 (.a(PC_q), .b(10'h1), .c_i(1'b0), .s(add_1_s));  // open: c_o
  Multiplexer #(.Bits(10)) multiplexer_1 (
    .sel(and_1_out), .in_0(add_1_s), .in_1({2'b00, IMM_value[7:5], ALU_Type, IMM_value[3:0]}),
    .out(multiplexer_1_out));
  and and_1 (and_1_out, CND_out, CND_en_flag);
  Register #(.Bits(10)) PC (.D(multiplexer_1_out), .C(CLK), .en(1'b1), .Q(PC_q));
  not not_1 (not_1_out, Data_in_selector[1]);
  not not_2 (not_2_out, Data_in_selector[0]);
  ROM #(.AddrBits(10), .Bits(10)) ROM (
    .A(PC_q), .sel(1'b1), .D({Data_in_selector, IMM_value[7:5], ALU_Type, IMM_value[3:0]}));
  and and_2 (ALU_en_flag, Data_in_selector[0], Data_in_selector[1]);
  or or_1 (NotCND, Data_in_selector[0], Data_in_selector[1]);
  and and_3 (IMM_en_flag, Data_in_selector[0], not_1_out);
  and and_4 (MOV_en_flag, not_2_out, Data_in_selector[1]);
  not not_3 (CND_en_flag, NotCND);
  Multiplexer #(.Bits(4)) multiplexer_2 (
    .sel(IMM_en_flag), .in_0(IMM_value[3:0]), .in_1(4'b0010), .out(multiplexer_2_out));
  Multiplexer #(.Bits(4)) multiplexer_3 (
    .sel(MOV_en_flag), .in_0(4'b0001), .in_1({IMM_value[7:5], ALU_Type}), .out(multiplexer_3_out));
  Comparator #(.Bits(4)) comparator_1 (.a(IMM_value[3:0]), .b(4'b0101), .eq(comparator_1_eq));  // open: gt, lt
  Comparator #(.Bits(4)) comparator_2 (
    .a({IMM_value[7:5], ALU_Type}), .b(4'b0101), .eq(comparator_2_eq));  // open: gt, lt
  Register #(.Bits(10)) register_1 (.D(REG_OUT1), .C(CLK), .en(ALU_en_flag), .Q(register_1_q));
  RegisterFile #(.AddrBits(4), .Bits(10)) registerfile_1 (
    .Din(DATA_IN_REG), .we(NotCND), .Rw(multiplexer_2_out), .C(CLK), .Ra(4'b0000), .Rb(multiplexer_3_out),
    .Da(REG_OUT1), .Db(REG_OUT2));
  Multiplexer #(.Selector_Bits(2), .Bits(10)) multiplexer_4 (
    .sel(Data_in_selector), .in_0({10{1'b0}}), .in_1({2'b00, IMM_value[7:5], ALU_Type, IMM_value[3:0]}),
    .in_2(REG_OUT2), .in_3(ALU_result), .out(multiplexer_4_out));
  and and_5 (and_5_out, comparator_1_eq, comparator_2_eq, MOV_en_flag);
  Multiplexer #(.Bits(10)) multiplexer_5 (.sel(and_5_out), .in_0(multiplexer_4_out), .in_1(Input), .out(DATA_IN_REG));
  Seven_Seg_Hex seven_seg_hex_1 (.d(register_1_q[7:4]), .dp(register_1_q[8]));
  Seven_Seg_Hex seven_seg_hex_2 (.d(register_1_q[3:0]), .dp(register_1_q[9]));
  Add #(.Bits(10)) add_2 (.a(REG_OUT1), .b(REG_OUT2), .c_i(1'b0), .s(add_2_s));  // open: c_o
  Sub #(.Bits(10)) sub_1 (.a(REG_OUT1), .b(REG_OUT2), .c_i(1'b0), .s(sub_1_s));  // open: c_o
  Comparator #(.Bits(10)) comparator_3 (.a(REG_OUT1), .b(REG_OUT2), .gt(CND_out));  // open: eq, lt
  Multiplexer #(.Bits(10)) multiplexer_6 (.sel(ALU_Type), .in_0(add_2_s), .in_1(sub_1_s), .out(ALU_result));

  // Other names for the same wires on the sheet: INSTRUCTION[9:0] = {Data_in_selector, IMM_value[7:5], ALU_Type, IMM_value[3:0]};
  //   JMP_ADDR[7:0] = {IMM_value[7:5], ALU_Type, IMM_value[3:0]}; Rd[3:0] = IMM_value[3:0]; IMM_value[4] = ALU_Type;
  //   Rs[3:0] = {IMM_value[7:5], ALU_Type}

  // Notes on the sheet:
  //   CLK: Hz: 10
  //   Input: default 2
  //   contents of ROM (hex, n*v repeats v):
  //   104,220,307,11b,255,221,250,4,251,220,4,153,220,307,e,0,0,300
endmodule
